# Fritzing sketch LevitronV1 (saved by Fritzing 0.9.0b)
breadboards: 1

parts:
  U1 = LM 358 Dual Op-Amp [package="DIP8 [THT]"]
  Bauteil1 = Arduino Nano (Rev3.0) [part_number="Arduino Nano"]
  C2 = Ceramic Capacitor [capacitance=10nF voltage=10V package="100 mil [THT, multilayer]"]
  J1 = longpad pin header, 6 pins [form="long pad"]
  J2 = longpad pin header, 3 pins [form="long pad"]
  J3 = screw terminal, 3 pins
  R2 = Resistor [tolerance=±5% resistance=2.2k package=THT]
  R3 = Resistor [tolerance=±5% resistance=47k package=THT]
  R1 = Resistor [tolerance=±5% resistance=2.2k package=THT]
  R4 = Resistor [tolerance=±5% resistance=2.2k package=THT]
  R5 = Resistor [tolerance=±5% resistance=2.2k package=THT]
  R6 = Resistor [tolerance=±5% resistance=47k package=THT]
  C1 = Ceramic Capacitor [capacitance=10nF package="100 mil [THT, multilayer]"]

nets:
  N1: U1.connector0, Bauteil1.A6, R3.Pin_1, C1.1
  N2: U1.connector1, R3.Pin_0, R1.Pin_1, C1.0
  N3: U1.connector2, R2.Pin_1
  GND: U1.connector3, Bauteil1.GND, J3.pin2
  N4: U1.connector4, R4.Pin_1
  N5: U1.connector5, C2.0, R5.Pin_1, R6.Pin_0
  N6: U1.connector6, Bauteil1.A7, C2.1, R6.Pin_1
  5V: U1.connector7, Bauteil1.5V, J3.pin3
  CoilY_N: Bauteil1.D5, J1.pin5
  CoilY_P: Bauteil1.D6, J1.pin4
  CoilX_N: Bauteil1.D7, J1.pin3
  CoilX_P: Bauteil1.D8, J1.pin2
  CoilYPower: Bauteil1.D9, J1.pin6
  CoilXPower: Bauteil1.D10, J1.pin1
  HallXOut: J2.pin1, R2.Pin_0
  Vref2V5: J2.pin2, R1.Pin_0, R5.Pin_0
  HallYOut: J2.pin3, R4.Pin_0

notes:
  Timer1 PWM
  IN1
  ENA
  IN2
  IN3
  IN4
  ENB
  HallXOut
  HallRefOut (2V5)
  HallYOut
  L298N Board
  DIY Levitron, Just another Project to make things fly, 0.2
